# Fritzing sketch saksi_2 (saved by Fritzing 0.9.3b)
circuit board: 10cm x 7cm

parts:
  Parça7 = NRF24L01+ Breakout Board
  IRFZ44N1 = MOSFET-NCHANNEL [package=to220v]
  IRFZ44N3 = MOSFET-NCHANNEL [package=to220v]
  1K_4 = Resistor [tolerance=±5% resistance=1k package=THT]
  Valf = Header 2 [package=jst-2-pth]
  Ekran_1 = Header 4 [package=jst-4-pth]
  Parça8 = Adafruit TCA9548A
  12_V = Power Jack [package=power_jack_pth_lock]
  Isitici = Header 2 [package=jst-2-pth]
  LED = Header 2 [package=jst-2-pth]
  Pompa = Header 2 [part_number=Pompa package=jst-2-pth]
  Ekran_2 = Header 4 [package=jst-4-pth]
  Depo_Sens = Header 3 [package=jst-3-pth]
  Nem_Sens = Header 3 [package=jst-3-pth]
  Sicaklik_Sens = Header 3 [package=jst-3-pth]
  Isik_Sens = Header 4 [package=jst-4-pth]
  1K_3 = Resistor [tolerance=±5% resistance=1k package=THT]
  1K_2 = Resistor [tolerance=±5% resistance=1k package=THT]
  1K_1 = Resistor [tolerance=±5% resistance=1k package=THT]
  D4 = Rectifier Diode [part_number=1N4001 package="300 mil [THT]"]
  D1 = Schottky Diode [part_number=1N5817 package="300 mil [THT]"]
  D2 = Schottky Diode [part_number=1N5817 package="300 mil [THT]"]
  D3 = Schottky Diode [part_number=1N5817 package="300 mil [THT]"]
  10K_1-2 = Resistor [tolerance=±5% resistance=1k package=THT]
  10K_4-2 = Resistor [tolerance=±5% resistance=1k package=THT]
  10K_2-2 = Resistor [tolerance=±5% resistance=1k package=THT]
  10K_3-2 = Resistor [tolerance=±5% resistance=1k package=THT]
  10K_3-1 = Resistor [tolerance=±5% resistance=10k package=THT]
  10K_1-1 = Resistor [tolerance=±5% resistance=10k package=THT]
  10K_4-1 = Resistor [tolerance=±5% resistance=10k package=THT]
  10K_2-1 = Resistor [tolerance=±5% resistance=10k package=THT]
  BC547_2 = NPN-Transistor [package="TO92 [THT]"]
  BC547_3 = NPN-Transistor [package="TO92 [THT]"]
  BC547_4 = NPN-Transistor [package="TO92 [THT]"]
  BC547_1 = NPN-Transistor [package="TO92 [THT]"]
  IRFZ44N2 = MOSFET-NCHANNEL [package=to220v]
  IRFZ44N4 = MOSFET-NCHANNEL [package=to220v]
  Parça1 = Arduino Nano (Rev3.0)
  ZS-042_RTC2 = ZS-042 RTC Module
  R1 = Resistor [tolerance=±5% resistance=4.7k package=THT]

nets:
  GND: Parça7.GND, Ekran_2.2, Depo_Sens.2, Nem_Sens.2, Sicaklik_Sens.2, Isik_Sens.4, Parça1.GND, ZS-042_RTC2.GND
  VCC: Parça7.VCC, Ekran_2.1, Depo_Sens.3, Nem_Sens.3, Sicaklik_Sens.3, Isik_Sens.3, Parça1.5V, Parça1.3V3, ZS-042_RTC2.VCC, R1.Pin_1
  N1: Parça7.CE, Parça1.D9
  N2: Parça7.CS, Parça1.D10
  N3: Parça7.SCK, Parça1.D13/SCK
  N4: Parça7.MOSI, Parça1.D11/MOSI
  N5: Parça7.MISO, Parça1.D12/MISO
  N6: Parça7.IRQ, Parça1.D2
  N7: IRFZ44N1.G, 10K_1-2.Pin_1, BC547_1.E
  N8: IRFZ44N1.D, Pompa.1, D1.anode
  N9: IRFZ44N1.S, IRFZ44N3.S, 12_V.GND, 10K_1-2.Pin_0, 10K_4-2.Pin_0, 10K_2-2.Pin_1, 10K_3-2.Pin_1, 10K_3-1.Pin_1, 10K_1-1.Pin_1, 10K_4-1.Pin_1, 10K_2-1.Pin_1, IRFZ44N2.S, IRFZ44N4.S
  N10: IRFZ44N3.G, 10K_3-2.Pin_0, BC547_3.E
  N11: IRFZ44N3.D, LED.1, D3.anode
  N12: 1K_4.Pin_0, Parça1.D8
  N13: 1K_4.Pin_1, 10K_4-1.Pin_0, BC547_4.B
  N14: Valf.1, D2.anode, IRFZ44N4.D
  N15: Valf.2, 12_V.PWR, Isitici.2, LED.2, Pompa.2, D4.cathode, D1.cathode, D2.cathode, D3.cathode, BC547_2.C, BC547_3.C, BC547_4.C, BC547_1.C
  N16: Ekran_1.1, Parça1.A0
  N17: Ekran_1.2, Parça1.A1
  N18: Parça8.5SDA, ZS-042_RTC2.SDA
  N19: Parça8.5SCL, ZS-042_RTC2.SCL
  N20: Parça8.6SDA, Isik_Sens.2
  N21: Parça8.6SCL, Isik_Sens.1
  N22: Parça8.7SDA, Ekran_2.4
  N23: Parça8.7SCL, Ekran_2.3
  N24: Parça8.INPUTSDA, Parça1.A4
  N25: Parça8.INPUTSCL, Parça1.A5
  N26: Isitici.1, D4.anode, IRFZ44N2.D
  N27: Depo_Sens.1, Sicaklik_Sens.1, Parça1.A6, Parça1.A2, R1.Pin_0
  N28: Nem_Sens.1, Parça1.A3
  N29: 1K_3.Pin_0, Parça1.D6
  N30: 1K_3.Pin_1, 10K_3-1.Pin_0, BC547_3.B
  N31: 1K_2.Pin_0, Parça1.D5
  N32: 1K_2.Pin_1, 10K_2-1.Pin_0, BC547_2.B
  N33: 1K_1.Pin_0, Parça1.D7
  N34: 1K_1.Pin_1, 10K_1-1.Pin_0, BC547_1.B
  N35: 10K_4-2.Pin_1, BC547_4.E, IRFZ44N4.G
  N36: 10K_2-2.Pin_0, BC547_2.E, IRFZ44N2.G

notes:
  A0>EKRAN1-1>POT
  A1>EKRAN1-2>SECME BUTONU
  D4>EKRAN1-3>ALTA KAYDIRMA BUTONU
  D3>EKRAN1-4>USTE KAYDIRMA BUTONU
  D5>ISITICI
  D6>LED
  D7>POMPA
  D8>VALF
  A2>SICAKLIK SENS.
  A3>TOPRAK NEM SENS.
  A6>DEPO SENS.
  A4>SDA
  A5>SCL
  SC5>REAL TIME CLOCK-SCL
  SD5>REAL TIME CLOCK-SDA
  SC6>ISIK SENS.-1>ISIK SENS.-SCL
  SD6>ISIK SENS.-2>ISIK SENS.-SDA
  SC7>EKRAN2-3>EKRAN-SCL
  SD7>EKRAN2-4>EKRAN-SDA
  D9>KABLOSUZ-CE(3)
  D10>KABLOSUZ-CSN(4)
  D11>KABLOSUZ-MOSI(6)
  D12>KABLOSUZ-MISO(7)
  D13>KABLOSUZ-SCK(5)
  A2>KABLOSUZ-IRQ(8)

custom parts:
  Adafruit TCA9548A: You just found the perfect I2C sensor, and you want to wire up two or three or more of them to your Arduino when you realize "Uh oh, this chip has a fixed I2C address, and from what I know about I2C, you cannot have two devices with the same address on the same SDA/SCL pins!" Are you out of luck? You would be, if you didn't have this ultra-cool TCA9548A 1-to-8 I2C multiplexer! Finally, a way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
